# Fritzing sketch arduino 1 (saved by Fritzing 0.9.3b)
breadboards: 1

parts:
  Part1 = Arduino Uno (Rev3)
  C1 = Electrolytic Capacitor [capacitance=220µF package="200 mil [THT, electrolytic]"]
  R1 = Resistor [tolerance=±0.05% resistance=250 package="0402 [SMD]"]

nets:
  N1: Part1.A5/SCL, R1.Pin_0
  N2: Part1.GND, C1.-
  N3: C1.+, R1.Pin_1
