# Fritzing sketch rpi sensor suite (saved by Fritzing 0.9.3b)
breadboards: 1

parts:
  Part1 = Humidity Temperature Sensor SHT15
  Raspberry_Pi_1 = Raspberry Pi 3 [part_number=RPI-3-V1.2]

nets:
  GND: Part1.GND, Raspberry_Pi_1.GND
  N1: Part1.SCL, Raspberry_Pi_1.GIPO22
  3V3: Part1.VCC, Raspberry_Pi_1.3v3, Raspberry_Pi_1.3V3
